// Logisim project current_cpu_design.circ as structural Verilog: 8 circuits, main circuit main
module main (
);

  wire and_1_out, clock_1_out, control_test_1_alusrc, control_test_1_mem_to_reg, control_test_1_memory_write,
       control_test_1_memread, control_test_1_regwrite;
  wire [1:0] control_test_1_aluop;
  wire [15:0] adder_1_out, alu_old_1_out_4, bit_extender_1_out, multiplexer_1_out, multiplexer_2_out,
       ram_1_data, reg8_1_read_data1, reg8_1_read_data2, register_1_q, rom_1_data;

  Clock clock_1 (.out(clock_1_out));
  and and_1 (and_1_out, clock_1_out, 1'b1);
  Register #(.width(16)) register_1 (.D(adder_1_out), .en(1'b1), .Q(register_1_q), .clk(and_1_out));  // open: clr
  Adder #(.width(16)) adder_1 (.a(16'h1), .b(register_1_q), .out(adder_1_out));  // open: cin, cout
  ROM #(.addrWidth(16), .dataWidth(16)) rom_1 (.addr(register_1_q), .data(rom_1_data), .sel(1'b1));
  control_test control_test_1 (
    .opcode(rom_1_data[15:12]), .AluSrc(control_test_1_alusrc), .regWrite(control_test_1_regwrite),
    .memRead(control_test_1_memread), .mem_to_reg(control_test_1_mem_to_reg),
    .memory_write(control_test_1_memory_write), .ALUOp(control_test_1_aluop));  // open: regDst
  reg8 reg8_1 (
    .Write(control_test_1_regwrite), .Write_register(rom_1_data[2:0]), .write_data(multiplexer_2_out),
    .clock(and_1_out), .read_register2(rom_1_data[8:6]), .read_register1(rom_1_data[5:3]),
    .read_data1(reg8_1_read_data1), .read_data2(reg8_1_read_data2));  // open: reset
  assign bit_extender_1_out = {{10{1'b0}}, rom_1_data[11:6]};  // Bit_Extender bit_extender_1
  Multiplexer #(.width(16), .enable("false")) multiplexer_1 (
    .in0(reg8_1_read_data2), .in1(bit_extender_1_out), .out(multiplexer_1_out), .sel(control_test_1_alusrc));
  ALU_old alu_old_1 (
    .in_1(reg8_1_read_data1), .in_2(multiplexer_1_out), .Operand(control_test_1_aluop),
    .out_4(alu_old_1_out_4));
  RAM #(.addrWidth(16), .dataWidth(16), .bus("separate")) ram_1 (
    .addr(alu_old_1_out_4), .din(reg8_1_read_data2), .data(ram_1_data), .str(control_test_1_memory_write),
    .clk(and_1_out), .ld(control_test_1_memread));  // open: sel, clr
  Multiplexer #(.width(16), .enable("false")) multiplexer_2 (
    .in0(alu_old_1_out_4), .in1(ram_1_data), .out(multiplexer_2_out), .sel(control_test_1_mem_to_reg));

  // Notes on the sheet:
  //   contents of rom_1 (hex, n*v repeats v):
  //   0 3280 3089 3283 41 b010 3101
endmodule

module control (
  input  bit_0,
  input  bit_1,
  output AorM,
  output m2r,
  output out_5
);

  wire and_2_out;

  and and_1 (m2r, ~bit_0, bit_1);  // AND_Gate
  and and_2 (and_2_out, ~bit_0, ~bit_1);  // AND_Gate
  not not_1 (AorM, and_2_out);
  or or_1 (out_5, ~bit_0, ~bit_1);  // OR_Gate
endmodule

module reg8 (
  input  Write,
  input  [2:0] Write_register,
  input  [15:0] write_data,
  input  clock,
  input  [2:0] read_register2,
  input  [2:0] read_register1,
  input  reset,
  output [15:0] read_data1,
  output [15:0] read_data2
);

  wire and_1_out, and_2_out, and_3_out, and_4_out, and_5_out, and_6_out, and_7_out, and_8_out,
       decoder_1_out0, decoder_1_out1, decoder_1_out2, decoder_1_out3, decoder_1_out4, decoder_1_out5,
       decoder_1_out6, decoder_1_out7;
  wire [15:0] register_1_q, register_2_q, register_3_q, register_4_q, register_5_q, register_6_q,
       register_7_q, register_8_q;

  Decoder #(.select(3), .enable("false")) decoder_1 (
    .out0(decoder_1_out0), .out1(decoder_1_out1), .out2(decoder_1_out2), .out3(decoder_1_out3),
    .out4(decoder_1_out4), .out5(decoder_1_out5), .out6(decoder_1_out6), .out7(decoder_1_out7),
    .sel(Write_register));
  and and_1 (and_1_out, Write, decoder_1_out0);
  and and_2 (and_2_out, Write, decoder_1_out1);
  and and_3 (and_3_out, Write, decoder_1_out2);
  and and_4 (and_4_out, Write, decoder_1_out3);
  and and_5 (and_5_out, Write, decoder_1_out4);
  and and_6 (and_6_out, Write, decoder_1_out5);
  and and_7 (and_7_out, Write, decoder_1_out6);
  and and_8 (and_8_out, Write, decoder_1_out7);
  Register #(.width(16)) register_1 (.D(write_data), .en(and_1_out), .Q(register_1_q), .clk(clock), .clr(reset));
  Register #(.width(16)) register_2 (.D(write_data), .en(and_2_out), .Q(register_2_q), .clk(clock), .clr(reset));
  Register #(.width(16)) register_3 (.D(write_data), .en(and_3_out), .Q(register_3_q), .clk(clock), .clr(reset));
  Register #(.width(16)) register_4 (.D(write_data), .en(and_4_out), .Q(register_4_q), .clk(clock), .clr(reset));
  Register #(.width(16)) register_5 (.D(write_data), .en(and_5_out), .Q(register_5_q), .clk(clock), .clr(reset));
  Register #(.width(16)) register_6 (.D(write_data), .en(and_6_out), .Q(register_6_q), .clk(clock), .clr(reset));
  Register #(.width(16)) register_7 (.D(write_data), .en(and_7_out), .Q(register_7_q), .clk(clock), .clr(reset));
  Register #(.width(16)) register_8 (.D(write_data), .en(and_8_out), .Q(register_8_q), .clk(clock), .clr(reset));
  Multiplexer #(.select(3), .width(16), .enable("false")) multiplexer_1 (
    .in0(register_1_q), .in1(register_2_q), .in2(register_3_q), .in3(register_4_q), .in4(register_5_q),
    .in5(register_6_q), .in6(register_7_q), .in7(register_8_q), .out(read_data1), .sel(read_register1));
  Multiplexer #(.select(3), .width(16), .enable("false")) multiplexer_2 (
    .in0(register_1_q), .in1(register_2_q), .in2(register_3_q), .in3(register_4_q), .in4(register_5_q),
    .in5(register_6_q), .in6(register_7_q), .in7(register_8_q), .out(read_data2), .sel(read_register2));
endmodule

module ALU_old (
  input  [15:0] in_1,
  input  [15:0] in_2,
  input  [1:0] Operand,
  output [15:0] out_4
);

  wire [15:0] adder_1_out, adder_2_out, and_1_out, or_1_out;

  Adder #(.width(16)) adder_1 (.a(in_1), .b(in_2), .out(adder_1_out));  // open: cin, cout
  Adder #(.width(16)) adder_2 (.a(in_1), .b(in_2), .out(adder_2_out));  // open: cin, cout
  assign and_1_out = in_1 & in_2;  // AND_Gate and_1, 16 bits wide
  assign or_1_out = in_1 | in_2;  // OR_Gate or_1, 16 bits wide
  Multiplexer #(.select(2), .width(16)) multiplexer_1 (
    .in0(adder_1_out), .in1(adder_2_out), .in2(and_1_out), .in3(or_1_out), .out(out_4), .sel(Operand),
    .en(1'b1));
endmodule

module control_test (
  input  [3:0] opcode,
  output regDst,
  output AluSrc,
  output regWrite,
  output memRead,
  output mem_to_reg,
  output memory_write,
  output [1:0] ALUOp
);

  wire and_2_out;

  and R_type (regDst, ~opcode[1], ~opcode[0]);  // AND_Gate
  and and_1 (mem_to_reg, ~opcode[3], opcode[1]);  // AND_Gate
  and and_2 (and_2_out, opcode[2], opcode[0]);
  not not_1 (ALUOp[0], opcode[2]);
  and sw (memory_write, ~opcode[3], opcode[2], opcode[1], ~opcode[0]);  // AND_Gate
  or or_1 (AluSrc, and_2_out, memory_write);
  or or_2 (regWrite, regDst, and_2_out);

  assign ALUOp[1] = opcode[3];
  assign memRead = mem_to_reg;

  // Notes on the sheet:
  //   0101 li
  //   0111 lw
  //   0110 sw
  //   last two digits 00 -> R type 00 + 10 and 11 or
endmodule

module ALU_NEW (
  input  [15:0] d1,
  input  [15:0] d2,
  input  [1:0] alusignal,
  output bltsignal,
  output [15:0] out_5
);

  wire [15:0] adder_1_out, and_1_out, or_1_out;

  Comparator #(.width(16), .mode("unsigned")) comparator_1 (.a(d1), .b(d2), .lt(bltsignal));  // open: gt, eq
  Adder #(.width(16)) adder_1 (.a(d1), .b(d2), .out(adder_1_out));  // open: cin, cout
  assign and_1_out = d1 & d2;  // AND_Gate and_1, 16 bits wide
  assign or_1_out = d1 | d2;  // OR_Gate or_1, 16 bits wide
  Multiplexer #(.select(2), .width(16)) multiplexer_1 (
    .in0(adder_1_out), .in1(and_1_out), .in2(or_1_out), .out(out_5), .sel(alusignal), .en(1'b1));  // open: in3
endmodule

module ALU_control (
  input  [1:0] Funct,
  input  [1:0] ALUOp,
  output [1:0] out_3
);

  wire comparator_1_eq;
  wire [1:0] subtractor_1_out;

  Subtractor #(.width(2)) subtractor_1 (.a(ALUOp), .b(2'b01), .out(subtractor_1_out));  // open: bin, bout
  Comparator #(.width(2)) comparator_1 (.a(ALUOp), .b(2'b00), .eq(comparator_1_eq));  // open: gt, lt
  Multiplexer #(.width(2), .enable("false")) multiplexer_1 (
    .in0(subtractor_1_out), .in1(Funct), .out(out_3), .sel(comparator_1_eq));
endmodule

module Mycontrol (
  input  in_1,
  input  in_2,
  input  in_3,
  input  in_4,
  output RegDst,
  output ALUSrc,
  output RegWrite,
  output MemRead,
  output MemWrite,
  output Branch,
  output Jump
);

  wire and_1_out, and_2_out, and_3_out, and_4_out, and_5_out, and_6_out, and_7_out, and_8_out, and_9_out,
       and_10_out, and_11_out, and_15_out, and_16_out, not_1_out, not_2_out, not_3_out, not_4_out, not_5_out,
       not_6_out, not_7_out, not_8_out, not_9_out, not_10_out, not_11_out, not_12_out, not_13_out,
       not_14_out, not_15_out, not_16_out, not_17_out, not_18_out, not_19_out, not_20_out, not_21_out,
       not_22_out, not_23_out, not_24_out, not_25_out, not_26_out, not_27_out, not_28_out, not_29_out,
       or_1_out;

  not not_1 (not_1_out, in_1);
  not not_2 (not_2_out, in_2);
  not not_3 (not_3_out, in_3);
  not not_4 (not_4_out, in_4);
  not not_5 (not_5_out, in_1);
  not not_6 (not_6_out, in_3);
  not not_7 (not_7_out, in_1);
  not not_8 (not_8_out, in_4);
  not not_9 (not_9_out, in_1);
  not not_10 (not_10_out, in_2);
  or or_1 (or_1_out, in_3, in_4);
  not not_11 (not_11_out, in_2);
  not not_12 (not_12_out, in_3);
  not not_13 (not_13_out, in_1);
  not not_14 (not_14_out, in_2);
  not not_15 (not_15_out, in_1);
  not not_16 (not_16_out, in_4);
  not not_17 (not_17_out, in_3);
  not not_18 (not_18_out, in_2);
  not not_19 (not_19_out, in_3);
  not not_20 (not_20_out, in_4);
  not not_21 (not_21_out, in_2);
  not not_22 (not_22_out, in_3);
  not not_23 (not_23_out, in_4);
  not not_24 (not_24_out, in_2);
  not not_25 (not_25_out, in_3);
  not not_26 (not_26_out, in_3);
  not not_27 (not_27_out, in_4);
  not not_28 (not_28_out, in_1);
  not not_29 (not_29_out, in_2);
  and and_1 (and_1_out, not_1_out, not_2_out, not_3_out, not_4_out);
  and and_2 (and_2_out, not_5_out, in_2, not_6_out, in_4);
  and and_3 (and_3_out, not_7_out, in_2, in_3, not_8_out);
  and and_4 (and_4_out, not_9_out, not_10_out, or_1_out);
  and and_5 (and_5_out, in_1, in_2, in_4);
  and and_6 (and_6_out, in_1, not_11_out, not_12_out);
  and and_7 (and_7_out, not_13_out, not_14_out);
  and and_8 (and_8_out, not_15_out, in_3, not_16_out);
  and and_9 (and_9_out, in_2, not_17_out, in_4);
  and and_10 (and_10_out, in_1, in_2, in_4);
  and and_11 (and_11_out, not_18_out, not_19_out, not_20_out);
  and and_12 (MemRead, in_1, not_21_out, not_22_out, not_23_out);
  and and_13 (MemWrite, in_1, not_24_out, not_25_out, in_4);
  and and_14 (Branch, in_2, not_26_out, not_27_out);
  and and_15 (and_15_out, not_28_out, in_2, in_3, in_4);
  and and_16 (and_16_out, in_1, not_29_out, in_3);
  or or_2 (RegDst, and_1_out, and_2_out, and_3_out);
  or or_3 (ALUSrc, and_4_out, and_5_out, and_6_out);
  or or_4 (RegWrite, and_7_out, and_8_out, and_9_out, and_10_out, and_11_out);
  or or_5 (Jump, and_15_out, and_16_out);
endmodule
